// Logisim project 8bitsProcesador.circ as structural Verilog: 2 circuits, main circuit main
module main (
  output out_1,
  output [7:0] out_2
);

  ALU alu_1 (.A(8'h1), .B(8'h3), .in_3(2'b00), .Zero(out_1), .ALU_Respuesta(out_2));
endmodule

module ALU (
  input  [7:0] A,
  input  [7:0] B,
  input  [1:0] in_3,
  output Zero,
  output [7:0] ALU_Respuesta
);

  wire [7:0] adder_1_out, and_1_out, or_1_out, subtractor_1_out;

  Adder adder_1 (.a(A), .b(B), .out(adder_1_out));  // open: cin, cout
  Subtractor subtractor_1 (.a(A), .b(B), .out(subtractor_1_out));  // open: bin, bout
  assign and_1_out = A & B;  // AND_Gate and_1, 8 bits wide
  assign or_1_out = A | B;  // OR_Gate or_1, 8 bits wide
  Multiplexer #(.select(2), .width(8)) multiplexer_1 (
    .in0(adder_1_out), .in1(subtractor_1_out), .in2(and_1_out), .in3(or_1_out), .out(ALU_Respuesta),
    .sel(in_3));  // open: en
  Comparator comparator_1 (.a({8{1'b0}}), .b(ALU_Respuesta), .eq(Zero));  // open: gt, lt
endmodule
